# Fritzing sketch DHT11Rele3Nano (saved by Fritzing 0.9.3b)
breadboards: 1

parts:
  Componente1 = Arduino Nano (Rev3.0)
  KY-1 = Keyes Relay [package=THT]
  Power_plug1 = Power plug
  LED1 = LEDs [package=led10mm]
  DHT11_1 = DHT11 module

nets:
  GND: Componente1.GND, KY-1.ground, DHT11_1.GND
  N1: Componente1.D2, DHT11_1.DATA
  N2: Componente1.D3, KY-1.signal
  5V: Componente1.5V, KY-1.power, DHT11_1.VCC
  N3: KY-1.C, Power_plug1.GND
  N4: KY-1.NO, LED1.C
  N5: Power_plug1.VCC, LED1.A

custom parts:
  Keyes Relay: The Keyes 5V relay module is suitable for SCM development, home appliance control. It uses a 5V~12V TIL control signal which can control DC / AC signal.
  LEDs: LEDs Standard schematic elements and footprints for 5mm, 3mm, 1206, and 0603 sized LEDs. 5mm - Spark Fun Electronics SKU : COM-00529 (and others)
  DHT11 module: DHT11 black pcb module
