# Fritzing sketch DS18x20Rele3RegulableNano (saved by Fritzing 0.9.3b)
breadboards: 1

parts:
  Componente1 = Arduino Nano (Rev3.0)
  KY-1 = Keyes Relay [package=THT]
  Power_plug1 = Power plug
  LED1 = LEDs [package=led10mm]
  DS1 = DS18B20 1-Wire Temperature Sensor [part_number=DS18B20]
  R1 = Resistor [tolerance=±5% resistance=4.7k package=THT]
  R2 = Rotary Potentiometer (Small) [maximum_resistance=100kΩ package=THT]

nets:
  GND: Componente1.GND, KY-1.ground, DS1.GND, R2.leg2
  N1: Componente1.D2, DS1.DQ, R1.Pin_1
  N2: Componente1.D3, KY-1.signal
  5V: Componente1.5V, KY-1.power, DS1.VDD, R1.Pin_0, R2.leg1
  N3: Componente1.A0, R2.wiper
  N4: KY-1.C, Power_plug1.GND
  N5: KY-1.NO, LED1.C
  N6: Power_plug1.VCC, LED1.A

custom parts:
  Keyes Relay: The Keyes 5V relay module is suitable for SCM development, home appliance control. It uses a 5V~12V TIL control signal which can control DC / AC signal.
  LEDs: LEDs Standard schematic elements and footprints for 5mm, 3mm, 1206, and 0603 sized LEDs. 5mm - Spark Fun Electronics SKU : COM-00529 (and others)
