# Fritzing sketch Rele3Nano (saved by Fritzing 0.9.3b)
breadboards: 1

parts:
  Componente1 = Arduino Nano (Rev3.0)
  KY-1 = Keyes Relay [package=THT]
  LED1 = LEDs [package=led10mm]
  Power_plug1 = Power plug

nets:
  N1: Componente1.GND, KY-1.ground
  N2: Componente1.D3, KY-1.signal
  N3: Componente1.5V, KY-1.power
  N4: KY-1.C, Power_plug1.GND
  N5: KY-1.NO, LED1.C
  N6: LED1.A, Power_plug1.VCC

custom parts:
  Keyes Relay: The Keyes 5V relay module is suitable for SCM development, home appliance control. It uses a 5V~12V TIL control signal which can control DC / AC signal.
  LEDs: LEDs Standard schematic elements and footprints for 5mm, 3mm, 1206, and 0603 sized LEDs. 5mm - Spark Fun Electronics SKU : COM-00529 (and others)
